# Fritzing sketch Circuit (saved by Fritzing 1.0.1rc)
circuit board: 8.46667cm x 5.64444cm
breadboards: 1

parts:
  Arduino_Pro_Micro_5V_16MHz = Arduino Pro Micro (Clone)
  U1_Hall_Effect_Sensor_Throttle = ACS712 [package=so08]
  U2_Hall_Effect_Sensor_Clutch = ACS712 [package=so08]
  HX711_Load_Cell_Amp = HX711 Weighing Sensor Module
  R1_1k_Resistor = Resistor [tolerance=±10% power=0.5W resistance=1k package=THT]
  R3_Brake_Resistor = Rotary Potentiometer (Small) [maximum_resistance=10kΩ knob_status=50% power=0.5W package=THT]
  S1_Load_Cell_50kg = Load Sensor - 50kg [part_number=SEN-10245]
  R2_1k_Resistor = Resistor [tolerance=±10% power=0.5W resistance=1k package=THT]

nets:
  GND: Arduino_Pro_Micro_5V_16MHz.GND, U1_Hall_Effect_Sensor_Throttle.GND, U2_Hall_Effect_Sensor_Clutch.GND, HX711_Load_Cell_Amp.GND, R3_Brake_Resistor.leg2
  N1: Arduino_Pro_Micro_5V_16MHz.D3, HX711_Load_Cell_Amp.DO/RX
  N2: Arduino_Pro_Micro_5V_16MHz.D5, HX711_Load_Cell_Amp.CK/TX
  N3: Arduino_Pro_Micro_5V_16MHz.A0, U1_Hall_Effect_Sensor_Throttle.VOUT
  N4: Arduino_Pro_Micro_5V_16MHz.A2, U2_Hall_Effect_Sensor_Clutch.VOUT
  N5: Arduino_Pro_Micro_5V_16MHz.A3, R3_Brake_Resistor.wiper
  VCC: Arduino_Pro_Micro_5V_16MHz.RAW, U1_Hall_Effect_Sensor_Throttle.VCC, U2_Hall_Effect_Sensor_Clutch.VCC, HX711_Load_Cell_Amp.VCC, R3_Brake_Resistor.leg1
  N6: HX711_Load_Cell_Amp.E+, R1_1k_Resistor.Pin_0, S1_Load_Cell_50kg.W
  N7: HX711_Load_Cell_Amp.E-, S1_Load_Cell_50kg.B, R2_1k_Resistor.Pin_0
  N8: HX711_Load_Cell_Amp.A+, R1_1k_Resistor.Pin_1, R2_1k_Resistor.Pin_1
  N9: HX711_Load_Cell_Amp.A-, S1_Load_Cell_50kg.R

custom parts:
  Load Sensor - 50kg: Half-wheatstone bridge Load Cell modified from the Fritzing Repo This load sensor, sometimes called a strain gauge, is the same one found in digital bathroom scales (you know, the ones you use in January for your New Year's resolutions, and then forget about a month later). This sensor can measure up to about 110 pounds.
